# Fritzing sketch I2C (saved by Fritzing 0.9.3b)

parts:
  Componente1 = Arduino Mega 2560 (Rev3)
  Componente2 = Arduino Mega 2560 (Rev3)

nets:
  N1: Componente1.D21/SCL, Componente1.SCL, Componente2.D21/SCL
  N2: Componente1.D20/SDA, Componente2.D20/SDA, Componente2.SDA
