# Fritzing sketch RFID (saved by Fritzing 0.9.3b)
breadboards: 1

parts:
  M1 = DOIT Esp32 DevKit v1 (30 pins long, 11 pins width) [part_number=ESP32S-PIN30]
  Componente1 = RFID-RC522-v3
  R1 = Resistor [tolerance=±5% resistance=100 package=THT]
  R2 = Resistor [tolerance=±5% resistance=100 package=THT]
  R3 = Resistor [tolerance=±5% resistance=100 package=THT]
  R4 = Resistor [tolerance=±5% resistance=100 package=THT]
  LED1 = LED - 5mm [color="Red (633nm)" package="5 mm [THT]"]
  LED2 = LED - 5mm [color="Red (633nm)" package="5 mm [THT]"]
  LED3 = LED - 5mm [color="Red (633nm)" package="5 mm [THT]"]
  LED4 = LED - 5mm [color="Red (633nm)" package="5 mm [THT]"]

nets:
  3V3: M1.3V3, Componente1.3.3V
  GND: M1.GND, Componente1.GND, R1.Pin_1, R3.Pin_1, R4.Pin_1
  N1: M1.D15, M1.D2
  N2: M1.D4, LED1.anode
  N3: M1.RX2, LED2.anode
  N4: M1.TX2, LED3.anode
  N5: M1.D5, LED4.anode
  N6: M1.D18, Componente1.SCK
  N7: M1.D19, Componente1.MISO
  N8: M1.D21, Componente1.SDA
  N9: M1.D22, Componente1.RST
  N10: M1.D23, Componente1.MOSI
  N11: R1.Pin_0, LED4.cathode
  N12: R2.Pin_0, LED3.cathode
  N13: R3.Pin_0, LED2.cathode
  N14: R4.Pin_0, LED1.cathode

custom parts:
  DOIT Esp32 DevKit v1 (30 pins long, 11 pins width): The DOIT Esp32 DevKit v1 is one of the development board created by DOIT to evaluate the ESP-WROOM-32 module. It is based on the ESP32 microcontroller that boasts Wifi, Bluetooth, Ethernet and Low Power support all in a single chip. (vanepp) made breadboard work, adjusted pin numbering and labels and reduced size of schematic and cleaned up pcb. This chip is 30pins long (2 x15) and 11 pins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
  RFID-RC522-v3: A simple China made RFID-RC522 Reader (6x4 cm); do check the pin labels, as this is a MFRC522 based clone.
